# Fritzing sketch gsm_circuit (saved by Fritzing 0.9.9b)

parts:
  M1 = DOIT Esp32 DevKit v1 (30 pins long, 11 pins width) [part_number=ESP32S-PIN30]
  Q1 = MOSFET-NCHANNEL [package=to220v]
  S1 = Toggle Switch [package=THT]
  TP1 = TP4056 [chip_label=TP4056 package="DIP (Dual Inline) [THT]"]
  VCC1 = Parallel 18650 battery
  Part1 = FC-28 Soil Hygrometer Module
  Part2 = FC-28 Soil Hygrometer Module - Probe
  R2 = Resistor [tolerance=±5% resistance=1k package="1206 [SMD]"]
  R1 = Resistor [tolerance=±5% resistance=1M package="1206 [SMD]"]
  M2 = 0.9v-5V booster usb output
  Part3 = Solar Cell
  USBTTL1 = Micro USB B Plug
  USBTTL2 = USB A Plug
  SIM800L1 = SIM800L
  C1 = Electrolytic Capacitor [capacitance=220µF voltage=6.3V package="200 mil [THT, electrolytic]"]

nets:
  N1: M1.GND, Q1.S, TP1.pin6, R1.Pin_1, M2.pin1, M2.pin4
  N2: M1.RX2, SIM800L1.TXD
  N3: M1.TX2, SIM800L1.RXD
  N4: M1.D5, R2.Pin_0
  N5: M1.VP, Part1.AO
  N6: Q1.G, R2.Pin_1, R1.Pin_0
  N7: Q1.D, SIM800L1.GND, C1.-
  N8: S1.L1, M2.pin2, SIM800L1.NET, C1.+
  N9: S1.COM, TP1.pin3
  N10: TP1.pin1, Part3.+
  N11: TP1.pin2, Part3.-
  N12: TP1.pin4, VCC1.+#3
  N13: TP1.pin5, VCC1.+#2
  N14: Part1.POS, Part2.POS
  N15: Part1.NEG, Part2.NEG
  N16: USBTTL1.usb, USBTTL2.usb

custom parts:
  DOIT Esp32 DevKit v1 (30 pins long, 11 pins width): The DOIT Esp32 DevKit v1 is one of the development board created by DOIT to evaluate the ESP-WROOM-32 module. It is based on the ESP32 microcontroller that boasts Wifi, Bluetooth, Ethernet and Low Power support all in a single chip. (vanepp) made breadboard work, adjusted pin numbering and labels and reduced size of schematic and cleaned up pcb. This chip is 30pins long (2 x15) and 11 pins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
  TP4056: A DIP stand-in part for whatever IC you want. With 6 pins on a 300mil dual inline package (DIP) footprint.
  Parallel 18650 battery: 2x 18650 battery pack (3.7 Volts)
  FC-28 Soil Hygrometer Module: The FC-28 is a soil hygrometer module that uses the Texas Instruments LM393 comparator chip to provide an analog measurement of soil humidity. The digital output is high when soil moisture is over a certain threshold, as determined by adjusting the potentiometer.
  FC-28 Soil Hygrometer Module - Probe: The FC-28 is a soil hygrometer module that uses the Texas Instruments LM393 comparator chip to provide an analog measurement of soil humidity.
  0.9v-5V booster usb output: 0.9 V ~ 5 V up 5 V DC - DC booster module.
  USB A Plug: USB A Plug breadboard only for documetnation purposes.
  SIM800L: SIM800L is a miniature cellular module which allows for GPRS transmission, sending and receiving SMS and making and receiving voice calls. Low cost and small footprint and quad band frequency support make this module perfect solution for any project that require long range connectivity. After connecting power module boots up, searches for cellular network and login automatically. On board LED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
